// Logisim project cdm16.circ as structural Verilog: 20 circuits, main circuit cdm16
module cdm16 (
  input  [15:0] data_in,
  input  EXC,
  input  [5:0] exc_vec,
  input  IRQ,
  input  [5:0] int_vec,
  input  clock,
  input  \wait ,
  output mem,
  output data_ins_prime,
  output rd_wr_prime,
  output [15:0] address,
  output word,
  output [15:0] data_out,
  output IAck
);

  wire _0op, _1op, _2op, alu2, alu3, alu3_ind, alu_asrtD, and_3_out, and_4_out, and_5_out, and_6_out,
       and_8_out, and_9_out, and_10_out, and_11_out, and_12_out, and_13_out, and_14_out, and_15_out,
       and_16_out, and_17_out, and_18_out, and_19_out, and_20_out, and_21_out, and_24_out, and_26_out,
       and_28_out, and_33_out, and_34_out, and_35_out, and_36_out, and_38_out, and_39_out, and_41_out,
       arith_carry, br_abs, br_abs_d, br_abs_nop, br_rel_n, br_rel_nop, br_rel_p, branch_logic_1_go, cin,
       clk, clk_inhibit, clk_no_inhibit, comparator_1_eq, comparator_2_eq, cout, CUT, d_ff_1_q, d_ff_2_q,
       d_ff_4_qn, d_ff_5_q, decoder_1_out0, decoder_1_out1, decoder_1_out2, decoder_1_out3, decoder_1_out4,
       decoder_1_out5, decoder_1_out6, decoder_1_out7, decoder_2_out0, decoder_2_out1, decoder_2_out2,
       decoder_2_out3, decoder_2_out4, decoder_2_out5, decoder_2_out6, decoder_2_out7, decoder_3_out0,
       decoder_3_out1, decoder_3_out2, decoder_3_out3, decoder_3_out4, decoder_3_out5, decoder_3_out6,
       decoder_3_out7, decoder_4_out0, decoder_4_out2, decoder_4_out5, decoder_4_out6, decoder_4_out7,
       demultiplexer_1_out0, di, ei, exc_trig_div_by_zero, exc_trig_invalid_inst, exc_trig_pc, exc_trig_sp,
       exc_triggered, fetch, fp_asrt0, halt, imm6, imm9, imm_asrt1, imm_asrtD, imm_extend_negative,
       imm_shift, inc_address, \int , int_en, io_phase, latch_int, mem2, mem3, multiplexer_9_out, nor_1_out,
       not_1_out, not_2_out, not_3_out, not_4_out, not_5_out, not_6_out, not_7_out, not_8_out, not_9_out,
       not_10_out, not_11_out, not_12_out, or_6_out, or_8_out, or_9_out, or_10_out, or_12_out, or_13_out,
       or_14_out, pc_asrt0, pc_asrtD, pc_inc, pc_latch, priority_encoder_1_gs, priority_encoder_3_gs,
       ps_asrtD, ps_latch_flags, ps_latch_word, r_asrt0, r_asrt1, r_asrtD, r_latch, reset_exc, shifts,
       sign_extend, sp_asrt0, sp_asrtD, sp_dec, sp_inc, sp_latch, undriven, wait_t, word_t;
  wire [0:0] or_7_out;
  wire [2:0] alu_func, alu_op_d0, alu_op_d1, alu_op_type, CVZN, exc_internal_vec, multiplexer_14_out,
       multiplexer_15_out, phase, priority_encoder_1_out, priority_encoder_2_out, priority_encoder_3_out,
       rs0, rs1;
  wire [2:1] imm6_d;
  wire [3:0] bit_extender_8_out, br_abs_flags_d, multiplexer_6_out, multiplexer_13_out, ps_flags;
  wire [3:3] br_rel_flags_d;
  wire [5:0] exc_vec_t, int_vec_t;
  wire [14:0] ps_register_1_out;
  wire [15:0] bit_extender_1_out, bit_extender_2_out, bit_extender_3_out, bit_extender_4_out,
       bit_extender_5_out, bit_extender_6_out, bit_extender_7_out, bus_control_1_to_bus,
       controlled_buffer_4_out, imm, multiplexer_1_out, multiplexer_2_out, multiplexer_3_out,
       multiplexer_4_out, multiplexer_5_out, multiplexer_7_out, or_3_out, or_4_out, pc_register_1_mon,
       pc_register_1_out, pull_resistor_1_node, pull_resistor_2_node, register_3_q, register_4_q,
       register_5_q, register_6_q, register_8_q, register_9_q, register_10_q, register_11_q, shifter_1_out,
       shifter_2_out, sp_register_1_mon, sp_register_1_out;
  wire [15:13] register_12_q;
  wire [27:0] multiplexer_17_out, rom_1_data, rom_2_data;

  D_Flip_Flop #(.trigger("low")) d_ff_1 (.clk(clock), .D(\wait ), .Q(d_ff_1_q));  // open: Qn, preset, en, reset
  and and_1 (clk_no_inhibit, clock, not_1_out);
  not not_1 (not_1_out, d_ff_1_q);
  Counter #(.width(3), .max('h7), .trigger("falling")) counter_1 (
    .load(CUT), .D(3'b000), .count(not_2_out), .Q(phase), .clk(clk));  // open: carry, clr
  not not_2 (not_2_out, CUT);
  Decoder #(.select(3), .enable("false")) decoder_1 (
    .out0(decoder_1_out0), .out1(decoder_1_out1), .out2(decoder_1_out2), .out3(decoder_1_out3),
    .out4(decoder_1_out4), .out5(decoder_1_out5), .out6(decoder_1_out6), .out7(decoder_1_out7),
    .sel(br_abs_flags_d[2:0]));
  Register #(.width(6)) register_1 (.D(exc_vec), .Q(exc_vec_t), .clk(EXC));  // open: en, clr
  Register #(.width(6)) register_2 (.D(int_vec), .Q(int_vec_t), .clk(IRQ));  // open: en, clr
  not not_3 (not_3_out, clk_inhibit);
  and and_2 (clk, not_3_out, clk_no_inhibit);
  Pull_Resistor pull_resistor_1 (.node(pull_resistor_1_node));
  Pull_Resistor pull_resistor_2 (.node(pull_resistor_2_node));
  and and_3 (and_3_out, decoder_1_out0, r_latch);
  and and_4 (and_4_out, r_asrtD, decoder_1_out0);
  D_Flip_Flop d_ff_2 (.Q(d_ff_2_q), .preset(exc_trig_sp), .reset(reset_exc));  // open: clk, D, Qn, en
  D_Flip_Flop d_ff_3 (.preset(exc_trig_pc), .reset(reset_exc));  // open: clk, D, Q, Qn, en
  nor nor_1 (nor_1_out, phase[0], phase[1], phase[2]);
  D_Flip_Flop #(.trigger("falling")) d_ff_4 (
    .clk(clk), .D(d_ff_4_qn), .Qn(d_ff_4_qn), .en(CUT));  // open: Q, preset, reset
  assign pull_resistor_1_node = decoder_2_out1 ? register_3_q : 16'bz;  // Controlled_Buffer controlled_buffer_1
  assign pull_resistor_1_node = decoder_2_out0 ? register_4_q : 16'bz;  // Controlled_Buffer controlled_buffer_2
  assign pull_resistor_2_node = decoder_3_out0 ? register_4_q : 16'bz;  // Controlled_Buffer controlled_buffer_3
  Register #(.width(16), .trigger("falling")) register_3 (
    .D(controlled_buffer_4_out), .en(and_5_out), .Q(register_3_q), .clk(clk));  // open: clr
  Register #(.width(16), .trigger("falling")) register_4 (
    .D(controlled_buffer_4_out), .en(and_3_out), .Q(register_4_q), .clk(clk));  // open: clr
  and and_5 (and_5_out, decoder_1_out1, r_latch);
  and and_6 (and_6_out, r_asrtD, decoder_1_out1);
  assign controlled_buffer_4_out = and_4_out ? register_4_q : 16'bz;  // Controlled_Buffer controlled_buffer_4
  Priority_Encoder priority_encoder_1 (
    .in1(d_ff_2_q), .in2(undriven), .in3(exc_trig_invalid_inst), .in4(exc_trig_div_by_zero), .in5(EXC),
    .out(priority_encoder_1_out), .gs(priority_encoder_1_gs));  // open: in0, in6, in7, en_in, en_out
  and and_7 (fetch, nor_1_out, d_ff_4_qn);
  assign pull_resistor_1_node = decoder_2_out2 ? register_5_q : 16'bz;  // Controlled_Buffer controlled_buffer_5
  assign pull_resistor_2_node = decoder_3_out1 ? register_3_q : 16'bz;  // Controlled_Buffer controlled_buffer_6
  assign pull_resistor_2_node = decoder_3_out2 ? register_5_q : 16'bz;  // Controlled_Buffer controlled_buffer_7
  Register #(.width(16), .trigger("falling")) register_5 (
    .D(controlled_buffer_4_out), .en(and_8_out), .Q(register_5_q), .clk(clk));  // open: clr
  and and_8 (and_8_out, decoder_1_out2, r_latch);
  and and_9 (and_9_out, r_asrtD, decoder_1_out2);
  assign controlled_buffer_4_out = and_9_out ? register_5_q : 16'bz;  // Controlled_Buffer controlled_buffer_8
  assign controlled_buffer_4_out = and_6_out ? register_3_q : 16'bz;  // Controlled_Buffer controlled_buffer_9
  assign pull_resistor_1_node = decoder_2_out3 ? register_6_q : 16'bz;  // Controlled_Buffer controlled_buffer_10
  assign pull_resistor_2_node = decoder_3_out3 ? register_6_q : 16'bz;  // Controlled_Buffer controlled_buffer_11
  Register #(.width(16), .trigger("falling")) register_6 (
    .D(controlled_buffer_4_out), .en(and_10_out), .Q(register_6_q), .clk(clk));  // open: clr
  and and_10 (and_10_out, decoder_1_out3, r_latch);
  and and_11 (and_11_out, decoder_1_out4, r_latch);
  and and_12 (and_12_out, r_asrtD, decoder_1_out3);
  and and_13 (and_13_out, r_asrtD, decoder_1_out4);
  assign controlled_buffer_4_out = and_12_out ? register_6_q : 16'bz;  // Controlled_Buffer controlled_buffer_12
  Register #(.width(3)) register_7 (
    .D(priority_encoder_1_out), .Q(exc_internal_vec), .clk(priority_encoder_1_gs));  // open: en, clr
  and and_14 (and_14_out, priority_encoder_1_gs, not_4_out);
  not not_4 (not_4_out, reset_exc);
  assign pull_resistor_1_node = decoder_2_out5 ? register_8_q : 16'bz;  // Controlled_Buffer controlled_buffer_13
  assign pull_resistor_1_node = decoder_2_out4 ? register_9_q : 16'bz;  // Controlled_Buffer controlled_buffer_14
  assign pull_resistor_2_node = decoder_3_out4 ? register_9_q : 16'bz;  // Controlled_Buffer controlled_buffer_15
  Register #(.width(16), .trigger("falling")) register_8 (
    .D(controlled_buffer_4_out), .en(and_15_out), .Q(register_8_q), .clk(clk));  // open: clr
  Register #(.width(16), .trigger("falling")) register_9 (
    .D(controlled_buffer_4_out), .en(and_11_out), .Q(register_9_q), .clk(clk));  // open: clr
  and and_15 (and_15_out, decoder_1_out5, r_latch);
  and and_16 (and_16_out, r_asrtD, decoder_1_out5);
  assign controlled_buffer_4_out = and_13_out ? register_9_q : 16'bz;  // Controlled_Buffer controlled_buffer_16
  assign bit_extender_1_out = {{13{1'b0}}, exc_internal_vec};  // Bit_Extender bit_extender_1
  assign bit_extender_2_out = {{10{1'b0}}, exc_vec_t};  // Bit_Extender bit_extender_2
  D_Flip_Flop #(.trigger("falling")) d_ff_5 (.clk(clk), .D(and_14_out), .Q(d_ff_5_q));  // open: Qn, preset, en, reset
  assign pull_resistor_1_node = decoder_2_out6 ? register_10_q : 16'bz;  // Controlled_Buffer controlled_buffer_17
  assign pull_resistor_2_node = decoder_3_out5 ? register_8_q : 16'bz;  // Controlled_Buffer controlled_buffer_18
  assign pull_resistor_2_node = decoder_3_out6 ? register_10_q : 16'bz;  // Controlled_Buffer controlled_buffer_19
  Register #(.width(16), .trigger("falling")) register_10 (
    .D(controlled_buffer_4_out), .en(and_17_out), .Q(register_10_q), .clk(clk));  // open: clr
  and and_17 (and_17_out, decoder_1_out6, r_latch);
  and and_18 (and_18_out, r_asrtD, decoder_1_out6);
  assign controlled_buffer_4_out = and_16_out ? register_8_q : 16'bz;  // Controlled_Buffer controlled_buffer_20
  assign controlled_buffer_4_out = and_18_out ? register_10_q : 16'bz;  // Controlled_Buffer controlled_buffer_21
  and and_19 (and_19_out, IRQ, int_en);
  assign bit_extender_3_out = {{10{1'b0}}, int_vec_t};  // Bit_Extender bit_extender_3
  Multiplexer #(.width(16), .enable("false")) multiplexer_1 (
    .in0(bit_extender_1_out), .in1(bit_extender_2_out), .out(multiplexer_1_out), .sel(comparator_1_eq));
  Comparator #(.width(3), .mode("unsigned")) comparator_1 (
    .a(exc_internal_vec), .b(3'b101), .eq(comparator_1_eq));  // open: gt, lt
  or or_1 (exc_triggered, priority_encoder_1_gs, d_ff_5_q);
  assign pull_resistor_1_node = decoder_2_out7 ? register_11_q : 16'bz;  // Controlled_Buffer controlled_buffer_22
  assign pull_resistor_2_node = decoder_3_out7 ? register_11_q : 16'bz;  // Controlled_Buffer controlled_buffer_23
  Register #(.width(16), .trigger("falling")) register_11 (
    .D(controlled_buffer_4_out), .en(and_20_out), .Q(register_11_q), .clk(clk));  // open: clr
  and and_20 (and_20_out, decoder_1_out7, r_latch);
  and and_21 (and_21_out, r_asrtD, decoder_1_out7);
  assign controlled_buffer_4_out = and_21_out ? register_11_q : 16'bz;  // Controlled_Buffer controlled_buffer_24
  and and_22 (IAck, fetch, and_19_out);
  or or_2 (latch_int, and_19_out, exc_triggered);
  and and_23 (reset_exc, exc_triggered, fetch);
  Multiplexer #(.width(16), .enable("false")) multiplexer_2 (
    .in0(bit_extender_3_out), .in1(multiplexer_1_out), .out(multiplexer_2_out), .sel(exc_triggered));
  assign or_3_out = multiplexer_2_out | 16'h8000;  // OR_Gate or_3, 16 bits wide
  assign bit_extender_4_out = {{7{1'b0}}, {alu_op_d0, imm6_d, br_abs_flags_d}};  // Bit_Extender bit_extender_4
  assign bit_extender_5_out = {{7{1'b1}}, {alu_op_d0, imm6_d, br_abs_flags_d}};  // Bit_Extender bit_extender_5
  assign bit_extender_6_out = {{10{1'b0}}, {alu_op_d0, imm6_d, br_abs_flags_d[3]}};  // Bit_Extender bit_extender_6
  assign bit_extender_7_out = {{10{1'b1}}, {alu_op_d0, imm6_d, br_abs_flags_d[3]}};  // Bit_Extender bit_extender_7
  assign pull_resistor_1_node = fp_asrt0 ? register_11_q : 16'bz;  // Controlled_Buffer controlled_buffer_25
  Multiplexer #(.width(16), .enable("false")) multiplexer_3 (
    .in0(controlled_buffer_4_out), .in1(or_3_out), .out(multiplexer_3_out), .sel(latch_int));
  not not_5 (not_5_out, fetch);
  Multiplexer #(.select(2), .width(16), .disabled(0), .enable("false")) multiplexer_4 (
    .in0(bit_extender_4_out), .in1(bit_extender_5_out), .in2(bit_extender_6_out), .in3(bit_extender_7_out),
    .out(multiplexer_4_out), .sel({imm6, imm_extend_negative}));
  Decoder #(.select(3), .disabled(0)) decoder_2 (
    .out0(decoder_2_out0), .out1(decoder_2_out1), .out2(decoder_2_out2), .out3(decoder_2_out3),
    .out4(decoder_2_out4), .out5(decoder_2_out5), .out6(decoder_2_out6), .out7(decoder_2_out7), .sel(rs0),
    .en(r_asrt0));
  Decoder #(.select(3), .disabled(0)) decoder_3 (
    .out0(decoder_3_out0), .out1(decoder_3_out1), .out2(decoder_3_out2), .out3(decoder_3_out3),
    .out4(decoder_3_out4), .out5(decoder_3_out5), .out6(decoder_3_out6), .out7(decoder_3_out7), .sel(rs1),
    .en(r_asrt1));
  Register #(.width(16), .trigger("falling")) register_12 (
    .D(multiplexer_3_out), .en(fetch),
    .Q({register_12_q, br_rel_flags_d[3], alu_op_d1, alu_op_d0, imm6_d, br_abs_flags_d}), .clk(clk),
    .clr(and_24_out));
  and and_24 (and_24_out, fetch, not_5_out);
  Shifter #(.width(16)) shifter_1 (.in(multiplexer_4_out), .\dist (4'b0001), .out(shifter_1_out));
  Decoder #(.select(3), .disabled(0), .enable("false")) decoder_4 (
    .out0(decoder_4_out0), .out1(_1op), .out2(decoder_4_out2), .out3(imm6), .out4(imm9),
    .out5(decoder_4_out5), .out6(decoder_4_out6), .out7(decoder_4_out7), .sel(register_12_q));
  Multiplexer #(.width(16), .disabled(0), .enable("false")) multiplexer_5 (
    .in0(multiplexer_4_out), .in1(shifter_1_out), .out(multiplexer_5_out), .sel(imm_shift));
  Shifter #(.width(16)) shifter_2 (.in(multiplexer_4_out), .\dist (4'b0010), .out(shifter_2_out));
  Comparator #(.width(3), .mode("unsigned")) comparator_2 (
    .a(phase), .b(3'b011), .eq(comparator_2_eq));  // open: gt, lt
  assign pull_resistor_1_node = sp_asrt0 ? sp_register_1_out : 16'bz;  // Controlled_Buffer controlled_buffer_26
  and and_25 (exc_trig_sp, sp_latch, controlled_buffer_4_out[0]);
  // Probe on sp_register_1_mon
  sp_register sp_register_1 (
    .In(controlled_buffer_4_out), .plus_2(sp_inc), .en(sp_latch), .minus_2(sp_dec), .clk(clk),
    .Mon(sp_register_1_mon), .Out(sp_register_1_out));  // open: clr
  assign pull_resistor_2_node = imm_asrt1 ? imm : 16'bz;  // Controlled_Buffer controlled_buffer_27
  assign controlled_buffer_4_out = imm_asrtD ? imm : 16'bz;  // Controlled_Buffer controlled_buffer_28
  Demultiplexer #(.disabled(0), .enable("false")) demultiplexer_1 (
    .out0(demultiplexer_1_out0), .out1(shifts), .in(decoder_4_out0), .sel(br_rel_flags_d[3]));
  Demultiplexer #(.select(2), .disabled(0), .enable("false")) demultiplexer_2 (
    .out0(_2op), .out1(alu3_ind), .out2(mem2), .out3(alu2), .in(decoder_4_out2),
    .sel({br_rel_flags_d[3], alu_op_d1[2]}));
  Demultiplexer #(.disabled(0), .enable("false")) demultiplexer_3 (
    .out0(mem3), .out1(alu3), .in(decoder_4_out5), .sel(br_rel_flags_d[3]));
  assign or_4_out = shifter_2_out | 16'h2;  // OR_Gate or_4, 16 bits wide
  and and_26 (and_26_out, \int , comparator_2_eq);
  assign controlled_buffer_4_out = sp_asrtD ? sp_register_1_out : 16'bz;  // Controlled_Buffer controlled_buffer_29
  Demultiplexer #(.disabled(0), .enable("false")) demultiplexer_4 (
    .out0(_0op), .out1(br_abs_d), .in(demultiplexer_1_out0), .sel(alu_op_d1[2]));
  Multiplexer #(.width(4), .enable("false")) multiplexer_6 (
    .in0({br_rel_flags_d[3], alu_op_d1}), .in1(br_abs_flags_d), .out(multiplexer_6_out), .sel(br_abs_d));
  Multiplexer #(.width(16), .disabled(0), .enable("false")) multiplexer_7 (
    .in0(shifter_2_out), .in1(or_4_out), .out(multiplexer_7_out), .sel(and_26_out));
  and and_27 (exc_trig_pc, pc_latch, controlled_buffer_4_out[0]);
  branch_logic branch_logic_1 (.cccc(multiplexer_6_out), .CVZN(ps_flags), .go(branch_logic_1_go));
  Multiplexer #(.width(16), .disabled(0), .enable("false")) multiplexer_8 (
    .in0(multiplexer_5_out), .in1(multiplexer_7_out), .out(imm), .sel(\int ));
  assign pull_resistor_1_node = pc_asrt0 ? pc_register_1_out : 16'bz;  // Controlled_Buffer controlled_buffer_30
  // Probe on pc_register_1_mon
  pc_register pc_register_1 (
    .In(controlled_buffer_4_out), .en(pc_latch), .plus_2(and_28_out), .Out(pc_register_1_out), .clk(clk),
    .Mon(pc_register_1_mon));  // open: clr
  and and_28 (and_28_out, pc_inc, not_9_out);
  not not_6 (not_6_out, br_abs);
  and and_29 (br_abs, br_abs_d, branch_logic_1_go);
  not not_7 (not_7_out, br_rel_n);
  and and_30 (br_rel_n, decoder_4_out6, branch_logic_1_go);
  not not_8 (not_8_out, br_rel_p);
  and and_31 (br_rel_p, decoder_4_out7, branch_logic_1_go);
  not not_9 (not_9_out, br_rel_nop);
  assign controlled_buffer_4_out = pc_asrtD ? pc_register_1_out : 16'bz;  // Controlled_Buffer controlled_buffer_31
  and and_32 (br_abs_nop, br_abs_d, not_6_out);
  and and_33 (and_33_out, decoder_4_out6, not_7_out);
  and and_34 (and_34_out, decoder_4_out7, not_8_out);
  Multiplexer #(.enable("false")) multiplexer_9 (
    .in0(and_35_out), .in1(cin), .out(multiplexer_9_out), .sel(arith_carry));
  alu alu_1 (
    .A(pull_resistor_1_node), .B(pull_resistor_2_node), .Cin(multiplexer_9_out), .func(alu_func),
    .op_type(alu_op_type), .C(cout), .V(CVZN[2]), .Z(CVZN[1]), .N(CVZN[0]), .S(address),
    .shift_count(alu_op_d0));
  or or_5 (br_rel_nop, and_33_out, and_34_out);
  and and_35 (and_35_out, mem, inc_address);
  assign controlled_buffer_4_out = alu_asrtD ? address : 16'bz;  // Controlled_Buffer controlled_buffer_32
  not not_10 (not_10_out, br_abs_flags_d[2]);
  or or_6 (or_6_out, alu_op_d1[0], alu_op_d1[1], alu_op_d1[2], br_rel_flags_d[3]);
  Multiplexer #(.width(3), .disabled(0), .enable("false")) multiplexer_10 (
    .in0(alu_op_d0), .in1(br_abs_flags_d[2:0]), .out(rs1), .sel(alu3_ind));
  Multiplexer #(.width(3), .disabled(0), .enable("false")) multiplexer_11 (
    .in0({imm6_d, br_abs_flags_d[3]}), .in1(br_abs_flags_d[2:0]), .out(rs0), .sel(imm6));
  or or_7 (or_7_out[0], alu3, alu3_ind);
  Decoder #(.select(2), .disabled(0)) decoder_5 (
    .out0(halt), .out1(wait_t), .out2(ei), .out3(di), .sel(br_abs_flags_d[1:0]), .en(and_36_out));
  and and_36 (and_36_out, not_10_out, br_abs_flags_d[3], _0op);
  and and_37 (\int , imm9, not_11_out);
  not not_11 (not_11_out, or_6_out);
  or or_8 (or_8_out, shifts, alu2, or_7_out[0]);
  // Probe on ps_flags
  ps_register ps_register_1 (
    .flags({cout, CVZN}), .word(controlled_buffer_4_out), .clk(clk),
    .out({int_en, ps_register_1_out[14:4], cin, ps_register_1_out[2:0]}), .out_flags(ps_flags),
    .latch_flags(ps_latch_flags), .latch_word(ps_latch_word), .ei(ei), .di(di));
  or or_9 (or_9_out, shifts, alu2);
  or or_10 (or_10_out, br_abs_nop, br_rel_nop);
  Multiplexer #(.width(3), .enable("false")) multiplexer_12 (
    .in0(3'b001), .in1({shifts, alu2, or_7_out[0]}), .out(alu_op_type), .sel(or_8_out));
  LED led_1 (.in(int_en));
  assign controlled_buffer_4_out = ps_asrtD ? {int_en, ps_register_1_out[14:4], cin, ps_register_1_out[2:0]} : 16'bz;  // Controlled_Buffer controlled_buffer_33
  Priority_Encoder priority_encoder_2 (
    .in0(_0op), .in1(_1op), .in2(_2op), .in3(mem2), .in4(imm6), .in5(imm9), .in6(mem3),
    .in7(priority_encoder_3_gs), .out(priority_encoder_2_out));  // open: en_in, gs, en_out
  Priority_Encoder priority_encoder_3 (
    .in0(br_abs), .in1(or_9_out), .in2(alu3_ind), .in3(alu3), .in4(br_rel_n), .in5(br_rel_p),
    .in6(or_10_out), .in7(fetch), .out(priority_encoder_3_out), .gs(priority_encoder_3_gs));  // open: en_in, en_out
  LED led_2 (.in(clk));
  LED led_3 (.in(clk_no_inhibit));
  assign bit_extender_8_out = {{1{1'b0}}, priority_encoder_3_out};  // Bit_Extender bit_extender_8
  Multiplexer #(.select(3), .width(4), .disabled(0), .enable("false")) multiplexer_13 (
    .in0(br_abs_flags_d), .in1({alu_op_d0[0], imm6_d, br_abs_flags_d[3]}), .in2({alu_op_d1[0], alu_op_d0}),
    .in3({alu_op_d1[0], alu_op_d0}), .in4({br_rel_flags_d[3], alu_op_d1}),
    .in5({br_rel_flags_d[3], alu_op_d1}), .in6({br_rel_flags_d[3], alu_op_d1}), .in7(bit_extender_8_out),
    .out(multiplexer_13_out), .sel(priority_encoder_2_out));
  and and_38 (and_38_out, alu_op_d1[1], alu_op_d1[2], br_rel_flags_d[3]);
  assign controlled_buffer_4_out = rd_wr_prime ? bus_control_1_to_bus : 16'bz;  // Controlled_Buffer controlled_buffer_34
  or or_11 (arith_carry, shifts, alu3);
  or or_12 (or_12_out, alu2, alu3_ind);
  and and_39 (and_39_out, imm6, and_38_out);
  Multiplexer #(.width(3), .enable("false")) multiplexer_14 (
    .in0(3'b101), .in1(3'b110), .out(multiplexer_14_out), .sel(and_39_out));
  bus_control bus_control_1 (
    .sign_extend(sign_extend), .odd_address(address[0]), .word(word_t), .clk_no_inhibit(clk_no_inhibit),
    .from_bus(controlled_buffer_4_out), .data_in(data_in), .inc_address(inc_address),
    .clk_inhibit(clk_inhibit), .data_out(data_out), .to_bus(bus_control_1_to_bus), .phase(io_phase));
  or or_13 (or_13_out, or_12_out, arith_carry);
  Multiplexer #(.width(3), .enable("false")) multiplexer_15 (
    .in0(alu_op_d1), .in1(alu_op_d0), .out(multiplexer_15_out), .sel(or_12_out));
  or or_14 (or_14_out, io_phase, clk_inhibit);
  not not_12 (not_12_out, or_14_out);
  Comparator #(.width(28)) comparator_3 (.a({28{1'b0}}), .b(rom_1_data), .eq(exc_trig_invalid_inst));  // open: gt, lt
  Multiplexer #(.width(3), .enable("false")) multiplexer_16 (
    .in0(multiplexer_14_out), .in1(multiplexer_15_out), .out(alu_func), .sel(or_13_out));
  and and_40 (word, word_t, not_12_out);
  ROM #(.addrWidth(10), .dataWidth(28)) rom_1 (
    .addr({phase, priority_encoder_2_out, multiplexer_13_out}), .data(rom_1_data));  // open: sel
  ROM #(.addrWidth(10), .dataWidth(28)) rom_2 (
    .addr({phase, priority_encoder_2_out, multiplexer_13_out}), .data(rom_2_data));  // open: sel
  Multiplexer #(.width(28), .enable("false")) multiplexer_17 (
    .in0(rom_1_data), .in1(rom_2_data), .out(multiplexer_17_out), .sel(exc_triggered));
  Multiplexer #(.width(28), .enable("false")) multiplexer_18 (
    .in0(multiplexer_17_out), .in1(28'h8000000),
    .out({CUT, word_t, sp_latch, sp_inc, sp_dec, sp_asrtD, sp_asrt0, sign_extend, rd_wr_prime, r_latch, r_asrtD, r_asrt1, r_asrt0, ps_latch_word, ps_latch_flags, ps_asrtD, pc_latch, pc_inc, pc_asrtD, pc_asrt0, mem, imm_shift, imm_extend_negative, imm_asrtD, imm_asrt1, fp_asrt0, data_ins_prime, alu_asrtD}),
    .sel(and_41_out));
  and and_41 (and_41_out, latch_int, fetch);

  // Other names for the same wires on the sheet: imm9_d[8:0] = {alu_op_d0, imm6_d, br_abs_flags_d};
  //   op_type_d0[3:0] = br_abs_flags_d; rd[2:0] = br_abs_flags_d[2:0]; rd_d[2:0] = br_abs_flags_d[2:0];
  //   data = data_ins_prime; read = rd_wr_prime; address_out[15:0] = address; CVZN[3] = cout; exc_trig_ext = EXC;
  //   imm6_d (some bits) = {alu_op_d0, br_abs_flags_d[3]};
  //   op_type_d1[3:0] = {alu_op_d0[0], imm6_d, br_abs_flags_d[3]}; rs0_d[2:0] = {imm6_d, br_abs_flags_d[3]};
  //   op_type_d2[3:0] = {alu_op_d1[0], alu_op_d0}; rs1_d[2:0] = alu_op_d0; shift_count_d[2:0] = alu_op_d0;
  //   br_rel_flags_d[2:0] = alu_op_d1; op_type_d3[3:0] = {br_rel_flags_d[3], alu_op_d1};
  //   XY[1:0] = {br_rel_flags_d[3], alu_op_d1[2]}; Y = alu_op_d1[2]; X = br_rel_flags_d[3]

  // Notes on the sheet:
  //   data_in: pull=down
  //   add halt and wait
  //   SP
  //   opt
  //   PС
  //   CVZN
  //   PS
  //   contents of rom_1 (hex, n*v repeats v):
  //   0 4a00282 d280882 5280882 ca01082 d284082 ca00282 d280882 4*c000000 0 0 ce00082 e280082 ca20082
  //   d2c0082 c0c0580 4a00282 8440000 a020000 8041000 8024000 8040200 8020800 6*0 804a001 15*0 c0c8082
  //   80c8082 81c8082 c0c8080 80c8080 81c8080 c028082 8028082 8*0 c0c00ce c0c00ee 80c00ce 80c00ee 81c00ce
  //   81c00ee c0200ce c0200ee 80200ce 80200ee 8040410 8040430 804a009 804a029 800a008 800a028 4a01082
  //   ca00092 ca000b2 a200049 a200069 11*0 c0d8082 80d8082 81d8082 c0d8080 80d8080 81d8080 c038082 8038082
  //   8*0 c080980 804a001 801a000 805a001 8000969 8000949 8000400 c080580 9*0 c080980 0 d284082 15*0
  //   8020800 60*0 4a00282 127*0 4080888 127*0 c084088
  //   contents of rom_2 (hex, n*v repeats v):
  //   1024*8000000
endmodule

module sp_register (
  input  [15:0] In,
  input  clr,
  input  clk,
  input  plus_2,
  input  en,
  input  minus_2,
  output [15:0] Out,
  output [15:0] Mon
);

  wire count, en_t;
  wire [15:0] incdec2_1_out, multiplexer_1_out;

  Multiplexer #(.width(16), .disabled(0), .enable("false")) multiplexer_1 (
    .in0(In), .in1(incdec2_1_out), .out(multiplexer_1_out), .sel(count));
  Register #(.width(16), .trigger("falling")) register_1 (
    .D(multiplexer_1_out), .en(en_t), .Q(Mon), .clk(clk), .clr(clr));
  or or_1 (count, plus_2, minus_2);
  or or_2 (en_t, count, en);
  incdec2 incdec2_1 (.in(Mon), .out(incdec2_1_out), .inc_dec_prime(plus_2));
  Multiplexer #(.width(16), .disabled(0), .enable("false")) multiplexer_2 (
    .in0(Mon), .in1(incdec2_1_out), .out(Out), .sel(minus_2));

  // Notes on the sheet:
  //   clk: pull=down
  //   minus_2: pull=down
  //   clr: pull=down
  //   en: pull=up
  //   plus_2: pull=down
endmodule

module pc_register (
  input  [15:0] In,
  input  clr,
  input  clk,
  input  en,
  input  plus_2,
  output [15:0] Out,
  output [15:0] Mon
);

  wire en_t;
  wire [15:0] incdec2_1_out, multiplexer_1_out;

  incdec2 incdec2_1 (.in(Mon), .out(incdec2_1_out));  // open: inc_dec_prime
  Register #(.width(16), .trigger("falling")) register_1 (
    .D(multiplexer_1_out), .en(en_t), .Q(Mon), .clk(clk), .clr(clr));
  Multiplexer #(.width(16), .disabled(0), .enable("false")) multiplexer_1 (
    .in0(In), .in1(incdec2_1_out), .out(multiplexer_1_out), .sel(plus_2));
  or or_1 (en_t, plus_2, en);

  assign Out = Mon;

  // Other names for the same wires on the sheet: count = plus_2

  // Notes on the sheet:
  //   en: pull=up
  //   clr: pull=down
  //   clk: pull=down
  //   plus_2: pull=down
endmodule

module ps_register (
  input  [3:0] flags,
  input  [15:0] word,
  input  clk,
  input  latch_word,
  input  latch_flags,
  input  ei,
  input  di,
  output [3:0] out_flags,
  output [15:0] out
);

  wire or_1_out, or_3_out, set_int_flag;
  wire [15:0] multiplexer_1_out, multiplexer_2_out;

  Multiplexer #(.width(16), .enable("false")) multiplexer_1 (
    .in0({out[15:4], flags}), .in1({ei, out[14:0]}), .out(multiplexer_1_out), .sel(set_int_flag));
  Multiplexer #(.width(16), .enable("false")) multiplexer_2 (
    .in0(multiplexer_1_out), .in1(word), .out(multiplexer_2_out), .sel(latch_word));
  or or_1 (or_1_out, latch_word, latch_flags);
  or or_2 (set_int_flag, ei, di);
  Register #(.width(16), .trigger("falling")) register_1 (
    .D(multiplexer_2_out), .en(or_3_out), .Q(out), .clk(clk));  // open: clr
  or or_3 (or_3_out, or_1_out, set_int_flag);
  Bit_Extender #(.in_width(16), .out_width(4)) bit_extender_1 (.in(out), .out(out_flags));

  // Notes on the sheet:
  //   word: pull=down
  //   clk: pull=down
  //   ei: pull=down
  //   flags: pull=down
  //   latch_flags: pull=down
  //   latch_word: pull=down
  //   di: pull=down
endmodule

module address_adder (
  input  [15:0] A,
  input  [15:0] B,
  output [16:0] Out
);

  Adder #(.width(16)) adder_1 (.a(A), .b(B), .out(Out[15:0]), .cout(Out[16]));  // open: cin

  // Notes on the sheet:
  //   B: pull=down
  //   A: pull=down
endmodule

module address_expander (
  input  [15:0] A,
  input  B,
  output [16:0] Out
);


  assign Out = {B, A};

  // Notes on the sheet:
  //   B: pull=down
  //   A: pull=down
endmodule

module incdec16 (
  input  [15:0] in,
  input  inc_dec_prime,
  output [15:0] out
);

  wire [15:0] multiplexer_1_out;

  Multiplexer #(.width(16), .enable("false")) multiplexer_1 (
    .in0({16{1'b1}}), .in1(16'h1), .out(multiplexer_1_out), .sel(inc_dec_prime));
  Adder #(.width(16)) adder_1 (.a(in), .b(multiplexer_1_out), .out(out));  // open: cin, cout

  // Notes on the sheet:
  //   inc_dec_prime: pull=up
endmodule

module incdec2 (
  input  [15:0] in,
  input  inc_dec_prime,
  output [15:0] out
);

  wire [15:0] multiplexer_1_out;

  Multiplexer #(.width(16), .enable("false")) multiplexer_1 (
    .in0(16'hfffe), .in1(16'h2), .out(multiplexer_1_out), .sel(inc_dec_prime));
  Adder #(.width(16)) adder_1 (.a(in), .b(multiplexer_1_out), .out(out));  // open: cin, cout

  // Notes on the sheet:
  //   inc_dec_prime: pull=up
endmodule

module bus_control (
  input  sign_extend,
  input  odd_address,
  input  word,
  input  clk_no_inhibit,
  input  [15:0] from_bus,
  input  [15:0] data_in,
  output inc_address,
  output clk_inhibit,
  output phase,
  output [15:0] data_out,
  output [15:0] to_bus
);

  wire and_1_out;
  wire [7:0] bit_extender_1_out, register_1_q;
  wire [15:0] bytes_swap_1_out, make_byte_2_out, multiplexer_1_out, multiplexer_3_out, multiplexer_5_out,
       n2s_compliment_1_out;

  Bit_Extender #(.in_width(16), .out_width(8)) bit_extender_1 (.in(data_in), .out(bit_extender_1_out));
  and and_1 (and_1_out, clk_inhibit, clk_no_inhibit);
  Register #(.trigger("falling")) register_1 (
    .D(bit_extender_1_out), .Q(register_1_q), .clk(and_1_out));  // open: en, clr
  and and_2 (clk_inhibit, odd_address, word);
  make_byte make_byte_1 ();  // open: In, Out
  Multiplexer #(.width(16), .disabled(0), .enable("false")) multiplexer_1 (
    .in0(from_bus), .in1(bytes_swap_1_out), .out(multiplexer_1_out), .sel(inc_address));
  bytes_swap bytes_swap_1 (.In(from_bus), .Out(bytes_swap_1_out));
  make_byte make_byte_2 (.In(data_in), .Out(make_byte_2_out));
  _2s_compliment u_2s_compliment_1 (.In(data_in), .Out(n2s_compliment_1_out));
  D_Flip_Flop #(.trigger("falling")) d_ff_1 (
    .clk(clk_no_inhibit), .D(clk_inhibit), .Q(inc_address));  // open: Qn, preset, en, reset
  Multiplexer #(.width(16), .disabled(0), .enable("false")) multiplexer_2 (
    .in0(from_bus), .in1(multiplexer_1_out), .out(data_out), .sel(word));
  Multiplexer #(.width(16), .disabled(0), .enable("false")) multiplexer_3 (
    .in0(make_byte_2_out), .in1(n2s_compliment_1_out), .out(multiplexer_3_out), .sel(sign_extend));
  Multiplexer #(.width(16), .disabled(0), .enable("false")) multiplexer_4 (
    .in0(multiplexer_3_out), .in1(multiplexer_5_out), .out(to_bus), .sel(word));
  Multiplexer #(.width(16), .disabled(0), .enable("false")) multiplexer_5 (
    .in0(data_in), .in1({bit_extender_1_out, register_1_q}), .out(multiplexer_5_out), .sel(inc_address));

  assign phase = inc_address;

  // Other names for the same wires on the sheet: odd = odd_address

  // Notes on the sheet:
  //   data_in: pull=down
endmodule

module alu (
  input  [15:0] A,
  input  [15:0] B,
  input  Cin,
  input  [2:0] func,
  input  [2:0] op_type,
  input  [2:0] shift_count,
  output C,
  output V,
  output Z,
  output N,
  output [15:0] S
);

  wire adc, add, adder16_1_cout, adder16_1_v, adder_carry, \and , and_3_out, and_4_out,
       barrel_shifter_1_cout, bic, multiplexer_7_out, multiplexer_8_out, neg, \not , \or , or_2_out,
       or_3_out, rcl, rcr, rol, ror, sbc, scl, shl, shr, shra, sub, sxt, \xor ;
  wire [15:0] adder16_1_s, and_1_out, and_2_out, barrel_shifter_1_out, make_byte_1_out, multiplexer_1_out,
       multiplexer_2_out, multiplexer_3_out, multiplexer_4_out, multiplexer_5_out, multiplexer_6_out,
       n2s_compliment_1_out, not_1_out, not_2_out, not_3_out, not_4_out, or_1_out, xor_1_out;

  Decoder #(.select(3), .disabled(0)) decoder_1 (
    .out0(\and ), .out1(\or ), .out2(\xor ), .out3(bic), .out4(add), .out5(adc), .out6(sub), .out7(sbc),
    .sel(func), .en(op_type[0]));
  Decoder #(.select(3), .disabled(0)) decoder_2 (
    .out0(neg), .out1(\not ), .out2(sxt), .out3(scl), .sel(func), .en(op_type[1]));  // open: out4, out5, out6, out7
  Decoder #(.select(3), .disabled(0)) decoder_3 (
    .out0(shl), .out1(shr), .out2(shra), .out3(rol), .out4(ror), .out5(rcl), .out6(rcr), .sel(func),
    .en(op_type[2]));  // open: out7
  assign and_1_out = A & B;  // AND_Gate and_1, 16 bits wide
  assign or_1_out = A | B;  // OR_Gate or_1, 16 bits wide
  assign xor_1_out = A ^ B;  // XOR_Gate xor_1, 16 bits wide
  assign and_2_out = A & not_1_out;  // AND_Gate and_2, 16 bits wide
  assign not_1_out = ~B;  // NOT_Gate not_1, 16 bits wide
  Multiplexer #(.width(16), .enable("false")) multiplexer_1 (
    .in0(A), .in1(not_2_out), .out(multiplexer_1_out), .sel(neg));
  assign not_2_out = ~A;  // NOT_Gate not_2, 16 bits wide
  Multiplexer #(.width(16), .enable("false")) multiplexer_2 (
    .in0(B), .in1(not_3_out), .out(multiplexer_2_out), .sel(or_2_out));
  assign not_3_out = ~B;  // NOT_Gate not_3, 16 bits wide
  or or_2 (or_2_out, sub, sbc);
  assign not_4_out = ~A;  // NOT_Gate not_4, 16 bits wide
  _2s_compliment u_2s_compliment_1 (.In(A), .Out(n2s_compliment_1_out));
  make_byte make_byte_1 (.In(A), .Out(make_byte_1_out));
  barrel_shifter barrel_shifter_1 (
    .In(A), .cin(Cin), .shift_type(func), .distance(shift_count), .Out(barrel_shifter_1_out),
    .cout(barrel_shifter_1_cout));
  adder16 adder16_1 (
    .A(multiplexer_1_out), .B(multiplexer_2_out), .S(adder16_1_s), .Cin(adder_carry), .Cout(adder16_1_cout),
    .V(adder16_1_v));
  Multiplexer #(.select(2), .width(16), .enable("false")) multiplexer_3 (
    .in0(adder16_1_s), .in1(not_4_out), .in2(n2s_compliment_1_out), .in3(make_byte_1_out),
    .out(multiplexer_3_out), .sel(func[1:0]));
  // NOT_Gate not_5 is placed but not wired
  Multiplexer #(.select(2), .width(16), .enable("false")) multiplexer_4 (
    .in0(and_1_out), .in1(or_1_out), .in2(xor_1_out), .in3(and_2_out), .out(multiplexer_4_out),
    .sel(func[1:0]));
  Multiplexer #(.width(16), .enable("false")) multiplexer_5 (
    .in0(multiplexer_4_out), .in1(adder16_1_s), .out(multiplexer_5_out), .sel(func[2]));
  and and_3 (and_3_out, sbc, Cin);
  or or_3 (or_3_out, and_3_out, and_4_out);
  and and_4 (and_4_out, Cin, adc);
  or or_4 (adder_carry, or_3_out, neg, sub);
  Multiplexer #(.width(16), .enable("false")) multiplexer_6 (
    .in0(multiplexer_5_out), .in1(multiplexer_3_out), .out(multiplexer_6_out), .sel(op_type[1]));
  Multiplexer #(.enable("false")) multiplexer_7 (
    .in0(adder16_1_cout), .in1(1'b0), .out(multiplexer_7_out), .sel(op_type[1]));
  Multiplexer #(.enable("false")) multiplexer_8 (
    .in0(adder16_1_v), .in1(1'b0), .out(multiplexer_8_out), .sel(op_type[1]));
  Multiplexer #(.width(16), .enable("false")) multiplexer_9 (
    .in0(multiplexer_6_out), .in1(barrel_shifter_1_out), .out({N, S[14:0]}), .sel(op_type[2]));
  Multiplexer #(.enable("false")) multiplexer_10 (
    .in0(multiplexer_7_out), .in1(barrel_shifter_1_cout), .out(C), .sel(op_type[2]));
  Multiplexer #(.enable("false")) multiplexer_11 (.in0(multiplexer_8_out), .in1(1'b0), .out(V), .sel(op_type[2]));
  // Probe on {N, S[14:0]}
  // NOT_Gate not_6 is placed but not wired
  zero16 zero16_1 (.in({N, S[14:0]}), .zero(Z));
  // NOT_Gate not_7 is placed but not wired

  assign S[15] = N;

  // Other names for the same wires on the sheet: _3op = op_type[0]; _2op = op_type[1]; shifts = op_type[2]

  // Notes on the sheet:
  //   func: pull=down
  //   A: pull=down
  //   Cin: pull=down
  //   B: pull=down
  //   shift_count: pull=down
  //   op_type: pull=down
endmodule

module multiplier (
  input  [15:0] A,
  input  [15:0] B,
  input  clk,
  input  reset,
  input  count,
  output [15:0] SLow,
  output [15:0] SHigh
);

  wire adder_1_cout, d_ff_1_q;
  wire [1:0] counter_1_q;
  wire [7:0] bit_extender_1_out, demultiplexer_1_out0, demultiplexer_1_out1, demultiplexer_1_out3,
       demultiplexer_2_out3, multiplexer_1_out, multiplexer_2_out, multiplexer_3_out, multiplexer_4_out;
  wire [15:0] adder_1_out, multiplier_1_out;

  assign bit_extender_1_out = {{7{1'b0}}, d_ff_1_q};  // Bit_Extender bit_extender_1
  Counter #(.width(2), .max('h3), .trigger("falling")) counter_1 (
    .count(count), .Q(counter_1_q), .clk(clk), .clr(reset));  // open: load, D, carry
  Multiplexer #(.select(2), .width(8), .enable("false")) multiplexer_1 (
    .in0(SLow[7:0]), .in1(SLow[15:8]), .in2(SLow[15:8]), .in3(SHigh[7:0]), .out(multiplexer_1_out),
    .sel(counter_1_q));
  Multiplexer #(.select(2), .width(8), .enable("false")) multiplexer_2 (
    .in0(SLow[15:8]), .in1(bit_extender_1_out), .in2(SHigh[7:0]), .in3(bit_extender_1_out),
    .out(multiplexer_2_out), .sel(counter_1_q));
  Adder #(.width(16)) adder_1 (
    .a(multiplier_1_out), .b({multiplexer_2_out, multiplexer_1_out}), .out(adder_1_out), .cout(adder_1_cout));  // open: cin
  D_Flip_Flop d_ff_1 (.clk(clk), .D(adder_1_cout), .Q(d_ff_1_q), .reset(reset));  // open: Qn, preset, en
  Multiplexer #(.width(8), .enable("false")) multiplexer_3 (
    .in0(A[7:0]), .in1(A[15:8]), .out(multiplexer_3_out), .sel(counter_1_q[0]));
  Register register_1 (.D(demultiplexer_1_out3), .en(count), .Q(SHigh[7:0]), .clk(clk), .clr(reset));
  Register register_2 (.D(demultiplexer_2_out3), .en(count), .Q(SHigh[15:8]), .clk(clk), .clr(reset));
  Multiplexer #(.width(8), .enable("false")) multiplexer_4 (
    .in0(B[7:0]), .in1(B[15:8]), .out(multiplexer_4_out), .sel(counter_1_q[1]));
  Multiplier multiplier_1 (
    .a(multiplexer_4_out), .b(multiplexer_3_out), .out(multiplier_1_out[7:0]), .cout(multiplier_1_out[15:8]));  // open: cin
  Register register_3 (.D(demultiplexer_1_out1), .en(count), .Q(SLow[15:8]), .clk(clk), .clr(reset));
  Demultiplexer #(.select(2), .width(8), .tristate("true"), .enable("false")) demultiplexer_1 (
    .out0(demultiplexer_1_out0), .out1(demultiplexer_1_out1), .out2(demultiplexer_1_out1),
    .out3(demultiplexer_1_out3), .in(adder_1_out[7:0]), .sel(counter_1_q));
  Demultiplexer #(.select(2), .width(8), .tristate("true"), .enable("false")) demultiplexer_2 (
    .out0(demultiplexer_1_out1), .out1(demultiplexer_1_out3), .out2(demultiplexer_1_out3),
    .out3(demultiplexer_2_out3), .in(adder_1_out[15:8]), .sel(counter_1_q));
  Register register_4 (.D(demultiplexer_1_out0), .en(count), .Q(SLow[7:0]), .clk(clk), .clr(reset));
endmodule

module barrel_shifter (
  input  [15:0] In,
  input  cin,
  input  [2:0] shift_type,
  input  [2:0] distance,
  output [15:0] Out,
  output cout
);

  wire [4:0] adder_1_out, bit_extender_1_out;
  wire [15:0] shifter_4_out, shifter_5_out;
  wire [16:0] shifter_1_out, shifter_2_out, shifter_3_out, shifter_6_out, shifter_7_out;

  assign bit_extender_1_out = {{2{1'b0}}, distance};  // Bit_Extender bit_extender_1
  Adder #(.width(5)) adder_1 (.a(bit_extender_1_out), .b(5'b00001), .out(adder_1_out));  // open: cin, cout
  Shifter #(.width(17)) shifter_1 (.in({{2{In[15]}}, In[14:0]}), .\dist (adder_1_out), .out(shifter_1_out));
  Shifter #(.width(17), .shift("lr")) shifter_2 (.in({In, In[0]}), .\dist (adder_1_out), .out(shifter_2_out));
  Shifter #(.width(17), .shift("ar")) shifter_3 (.in({In, In[0]}), .\dist (adder_1_out), .out(shifter_3_out));
  Shifter #(.width(16), .shift("rl")) shifter_4 (.in(In), .\dist (adder_1_out[3:0]), .out(shifter_4_out));
  Shifter #(.width(16), .shift("rr")) shifter_5 (.in(In), .\dist (adder_1_out[3:0]), .out(shifter_5_out));
  Shifter #(.width(17), .shift("rl")) shifter_6 (.in({cin, In}), .\dist (adder_1_out), .out(shifter_6_out));
  Shifter #(.width(17), .shift("rr")) shifter_7 (.in({In, cin}), .\dist (adder_1_out), .out(shifter_7_out));
  Multiplexer #(.select(3), .width(16), .enable("false")) multiplexer_1 (
    .in0(shifter_1_out[15:0]), .in1(shifter_2_out[16:1]), .in2(shifter_3_out[16:1]), .in3(shifter_4_out),
    .in4(shifter_5_out), .in5(shifter_6_out[15:0]), .in6(shifter_7_out[16:1]), .out(Out), .sel(shift_type));  // open: in7
  Multiplexer #(.select(3), .enable("false")) multiplexer_2 (
    .in0(shifter_1_out[16]), .in1(shifter_2_out[0]), .in2(shifter_3_out[0]), .in3(shifter_4_out[0]),
    .in4(shifter_5_out[15]), .in5(shifter_6_out[16]), .in6(shifter_7_out[0]), .out(cout), .sel(shift_type));  // open: in7

  // Other names for the same wires on the sheet: value[15:0] = In; type[2:0] = shift_type

  // Notes on the sheet:
  //   shift_type: pull=down
  //   In: pull=down
  //   distance: pull=down
  //   cin: pull=down
  //   shl
  //   shr
  //   shra
  //   rol
  //   ror
  //   rcl
  //   rcr
endmodule

module adder16 (
  input  Cin,
  input  [15:0] A,
  input  [15:0] B,
  output [15:0] S,
  output Cout,
  output V
);

  wire [15:0] and_1_out, and_2_out, and_3_out;
  wire [15:1] or_1_out;

  // Probe on A
  // Probe on B
  assign S = A ^ {or_1_out, Cin} ^ B;  // XOR_Gate xor_1, 16 bits wide
  assign and_1_out = B & A;  // AND_Gate and_1, 16 bits wide
  assign and_2_out = B & {or_1_out, Cin};  // AND_Gate and_2, 16 bits wide
  assign and_3_out = A & {or_1_out, Cin};  // AND_Gate and_3, 16 bits wide
  assign {Cout, or_1_out} = and_1_out | and_2_out | and_3_out;  // OR_Gate or_1, 16 bits wide
  // Probe on S
  xor xor_2 (V, or_1_out[15], Cout);

  // Notes on the sheet:
  //   B: pull=down
  //   Cin: pull=down
  //   A: pull=down
endmodule

module adder8 (
  input  Cin,
  input  [7:0] A,
  input  [7:0] B,
  output [7:0] S,
  output Cout,
  output V
);

  wire [7:0] and_1_out, and_2_out, and_3_out;
  wire [7:1] or_1_out;

  // Probe on A
  // Probe on B
  assign S = A ^ {or_1_out, Cin} ^ B;  // XOR_Gate xor_1, 8 bits wide
  assign and_1_out = B & A;  // AND_Gate and_1, 8 bits wide
  assign and_2_out = B & {or_1_out, Cin};  // AND_Gate and_2, 8 bits wide
  assign and_3_out = A & {or_1_out, Cin};  // AND_Gate and_3, 8 bits wide
  assign {Cout, or_1_out} = and_1_out | and_2_out | and_3_out;  // OR_Gate or_1, 8 bits wide
  // Probe on S
  xor xor_2 (V, or_1_out[7], Cout);

  // Notes on the sheet:
  //   B: pull=down
  //   A: pull=down
  //   Cin: pull=down
endmodule

module branch_logic (
  input  [3:0] cccc,
  input  [3:0] CVZN,
  output go
);

  wire and_1_out, and_2_out, and_3_out, and_4_out, and_5_out, and_6_out, and_7_out, decoder_1_out0,
       decoder_1_out1, decoder_1_out2, decoder_1_out3, decoder_2_out0, decoder_2_out1, decoder_2_out2,
       decoder_2_out3, not_1_out, not_2_out, or_1_out, xnor_1_out;

  not not_1 (not_1_out, cccc[3]);
  Decoder #(.select(2), .disabled(0)) decoder_1 (
    .out0(decoder_1_out0), .out1(decoder_1_out1), .out2(decoder_1_out2), .out3(decoder_1_out3),
    .sel(cccc[2:1]), .en(not_1_out));
  and and_1 (and_1_out, decoder_1_out0, CVZN[1]);
  and and_2 (and_2_out, decoder_1_out1, CVZN[3]);
  and and_3 (and_3_out, decoder_1_out2, CVZN[0]);
  and and_4 (and_4_out, decoder_1_out3, CVZN[2]);
  not not_2 (not_2_out, CVZN[1]);
  xnor xnor_1 (xnor_1_out, CVZN[0], CVZN[2]);
  Decoder #(.select(2), .disabled(0)) decoder_2 (
    .out0(decoder_2_out0), .out1(decoder_2_out1), .out2(decoder_2_out2), .out3(decoder_2_out3),
    .sel(cccc[2:1]), .en(cccc[3]));
  and and_5 (and_5_out, decoder_2_out0, not_2_out, CVZN[3]);
  and and_6 (and_6_out, xnor_1_out, decoder_2_out1);
  and and_7 (and_7_out, not_2_out, xnor_1_out, decoder_2_out2);
  or or_1 (or_1_out, and_1_out, and_2_out, and_3_out, and_4_out, and_5_out, and_6_out, and_7_out, decoder_2_out3);
  xor xor_1 (go, cccc[0], or_1_out);

  // Notes on the sheet:
  //   N
  //   Z
  //   V
  //   C
  //   EQ
  //   HS/CS
  //   MI
  //   VS
  //   N=V
  //   Z'
  //   HI
  //   GE
  //   GT
  //   <always>
endmodule

module zero8 (
  input  [7:0] in,
  output zero
);

  nor nor_1 (zero, in[0], in[1], in[2], in[3], in[4], in[5], in[6], in[7]);
endmodule

module zero16 (
  input  [15:0] in,
  output zero
);

  wire nor_1_out, nor_2_out;

  nor nor_1 (nor_1_out, in[0], in[1], in[2], in[3], in[4], in[5], in[6], in[7]);
  nor nor_2 (nor_2_out, in[8], in[9], in[10], in[11], in[12], in[13], in[14], in[15]);
  and and_1 (zero, nor_1_out, nor_2_out);
endmodule

module _2s_compliment (
  input  [15:0] In,
  output [15:0] Out
);

  wire [7:0] bit_extender_1_out;

  Bit_Extender #(.in_width(16), .out_width(8)) bit_extender_1 (.in(In), .out(bit_extender_1_out));
  assign Out = {{8{bit_extender_1_out[7]}}, bit_extender_1_out};  // Bit_Extender bit_extender_2
endmodule

module make_byte (
  input  [15:0] In,
  output [15:0] Out
);

  wire [7:0] bit_extender_1_out;

  Bit_Extender #(.in_width(16), .out_width(8)) bit_extender_1 (.in(In), .out(bit_extender_1_out));
  assign Out = {{8{1'b0}}, bit_extender_1_out};  // Bit_Extender bit_extender_2
endmodule

module bytes_swap (
  input  [15:0] In,
  output [15:0] Out
);


  assign Out = {In[7:0], In[15:8]};
endmodule
