// Logisim project test_circuit.circ as structural Verilog: 1 circuit, main circuit main
module main (
  output [7:0] r0,
  output [7:0] r1,
  output [7:0] r2,
  output [7:0] r3,
  output [15:0] pc,
  output [7:0] sp,
  output [7:0] ps,
  output halt
);

  wire cdm_8_mark5_1_p10, cdm_8_mark5_1_p11, cdm_8_mark5_1_p12, clock_1_out, decoder_1_out0, decoder_1_out1,
       not_1_out;
  wire [7:0] cdm_8_mark5_1_p14, cdm_8_mark5_1_p15, controlled_buffer_1_out;
  wire [15:0] cdm_8_mark5_1_p13;
  wire [15:8] pull_resistor_2_node, rom_1_p3;

  Clock clock_1 (.out(clock_1_out));
  // CdM_8_mark5 cdm_8_mark5_1: pin names not known; wires that end beside it: r0, r1, clock_1_out, r2, r3, halt, pc, sp, ps, cdm_8_mark5_1_p10, cdm_8_mark5_1_p11, cdm_8_mark5_1_p12, cdm_8_mark5_1_p13, cdm_8_mark5_1_p14, cdm_8_mark5_1_p15
  Decoder #(.disabled(0)) decoder_1 (
    .out0(decoder_1_out0), .out1(decoder_1_out1), .sel(cdm_8_mark5_1_p10), .en(cdm_8_mark5_1_p11));
  not not_1 (not_1_out, cdm_8_mark5_1_p12);
  assign controlled_buffer_1_out = not_1_out ? cdm_8_mark5_1_p14 : 8'bz;  // Controlled_Buffer controlled_buffer_1
  assign cdm_8_mark5_1_p15 = cdm_8_mark5_1_p12 ? controlled_buffer_1_out : 8'bz;  // Controlled_Buffer controlled_buffer_2
  // ROM rom_1: pin names not known; wires that end beside it: cdm_8_mark5_1_p13, decoder_1_out0, {rom_1_p3, controlled_buffer_1_out}
  Pull_Resistor pull_resistor_1 (.node(rom_1_p3));
  Pull_Resistor pull_resistor_2 (.node(pull_resistor_2_node));
  // RAM ram_1: pin names not known; wires that end beside it: cdm_8_mark5_1_p13[7:0], decoder_1_out1, clock_1_out, cdm_8_mark5_1_p12, {pull_resistor_2_node, controlled_buffer_1_out}
endmodule
